# Fritzing sketch SignBot (saved by Fritzing 0.9.3b)
breadboards: 1

parts:
  Board_0 = Arduino Uno (Rev3) - ICSP
  Board_2 = Arduino Uno (Rev3) - ICSP
  L_Pinky = Dagu DGServo 9g header connector (female) [package=THT]
  L_Ring = Dagu DGServo 9g header connector (female) [package=THT]
  L_Middle = Dagu DGServo 9g header connector (female) [package=THT]
  L_Thumb = Dagu DGServo 9g header connector (female) [package=THT]
  L_Index = Dagu DGServo 9g header connector (female) [package=THT]
  L_Pinky1 = Dagu DGServo 9g header connector (female) [package=THT]
  L_Thumb1 = Dagu DGServo 9g header connector (female) [package=THT]
  L_Ring1 = Dagu DGServo 9g header connector (female) [package=THT]
  L_Middle1 = Dagu DGServo 9g header connector (female) [package=THT]
  L_Index1 = Dagu DGServo 9g header connector (female) [package=THT]
  LL_winch = Dagu DGServo 9g header connector (female) [package=THT]
  LR_winch = Dagu DGServo 9g header connector (female) [package=THT]
  RR_winch = Dagu DGServo 9g header connector (female) [package=THT]
  RL_winch3 = Dagu DGServo 9g header connector (female) [package=THT]

nets:
  N1: Board_0.D8, LR_winch.pulse
  N2: Board_0.D9_PWM, LL_winch.pulse
  GND: Board_0.GND, Board_2.GND, L_Pinky.gnd, L_Ring.gnd, L_Middle.gnd, L_Pinky1.gnd, L_Thumb1.gnd, L_Ring1.gnd, L_Middle1.gnd, L_Index1.gnd, LL_winch.gnd, LR_winch.gnd
  N3: Board_0.D3_PWM, L_Thumb.pulse
  N4: Board_0.D4, L_Ring.pulse
  N5: Board_0.D5_PWM, L_Middle.pulse
  N6: Board_0.D6_PWM, L_Index.pulse
  N7: Board_0.D7, L_Pinky.pulse
  N8: Board_2.D8, RL_winch3.pulse
  N9: Board_2.D9_PWM, RR_winch.pulse
  N10: Board_2.D3_PWM, L_Pinky1.pulse
  N11: Board_2.D4, L_Ring1.pulse
  N12: Board_2.D5_PWM, L_Middle1.pulse
  N13: Board_2.D6_PWM, L_Thumb1.pulse
  N14: Board_2.D7, L_Index1.pulse
  VCC: L_Pinky.Vcc, L_Ring.Vcc, L_Middle.Vcc
  GND_2: L_Thumb.gnd, L_Index.gnd
  VCC_2: L_Thumb.Vcc, L_Index.Vcc
  VCC_3: L_Pinky1.Vcc, L_Thumb1.Vcc, L_Ring1.Vcc, L_Middle1.Vcc, L_Index1.Vcc, LL_winch.Vcc, LR_winch.Vcc
  GND_3: RR_winch.gnd, RL_winch3.gnd
  VCC_4: RR_winch.Vcc, RL_winch3.Vcc
